# Fritzing sketch pong (saved by Fritzing 0.9.3b)
circuit board: 6.5cm x 5.64444cm
perfboards: 1

parts:
  Part3 = Arduino Nano (Rev3.0)
  RCA3 = RCA [package=pth]
  R6 = Resistor [tolerance=±5% resistance=1k package=THT]  # not connected
  R7 = Resistor [tolerance=±5% resistance=470 package=THT]
  J5 = male pin header, 4 pins [form="♂ (male)"]
  J6 = male pin header, 4 pins [form="♂ (male)"]
  R8 = Resistor [tolerance=±5% resistance=220 package=THT]  # not connected
  LED2 = LED - 5mm [color="Red (633nm)" package="5 mm [THT]"]  # not connected

nets:
  N1: Part3.GND, RCA3.SHELL
  N2: Part3.D3, J6.pin3
  N3: Part3.D5, J5.pin3
  N4: Part3.D7, R7.Pin_1
  N5: Part3.5V, J5.pin2
